# Fritzing sketch hardware-design (saved by Fritzing 0.9.3b)
breadboards: 1

parts:
  Part1 = Arduino Mega 2560 (Rev3)
  R1 = Resistor [tolerance=±5% resistance=220 package="0402 [SMD]"]
  R2 = Resistor [tolerance=±5% resistance=220 package="0402 [SMD]"]
  R3 = Photocell (LDR) [package=THT]
  R4 = Photocell (LDR) [package=THT]
  R5 = Resistor [tolerance=±5% resistance=220 package="0402 [SMD]"]
  R6 = Resistor [tolerance=±5% resistance=220 package="0402 [SMD]"]
  J1 = Basic Servo
  U1 = NodeMCU V1.0
  Part2 = Solar Cell

nets:
  N1: Part1.A0, R1.Pin_0, R2.Pin_0
  N2: Part1.A1, R3.pin_1, R5.Pin_1
  N3: Part1.A2, R4.pin_1, R6.Pin_1
  N4: Part1.D11_PWM, U1.D2
  N5: Part1.D10_PWM, U1.D3
  5V: Part1.5V, R3.pin_0, R4.pin_0, J1.vcc
  GND: Part1.GND, R2.Pin_1, R5.Pin_0, R6.Pin_0, J1.gnd, U1.GND, Part2.-
  VIN: Part1.VIN, U1.Vin
  N6: Part1.D3_PWM, J1.pulse
  N7: R1.Pin_1, Part2.+

custom parts:
  NodeMCU V1.0: ESP8266 based NodeMCU
